// Logisim project alu.circ as structural Verilog
module aluReloaded (
  input  [7:0] A,
  input  [7:0] B,
  input  [7:0] C,
  input  [7:0] D,
  output [7:0] F,
  output [7:0] E
);

  wire [7:0] multiplexer_1_out, multiplexer_2_out;

  Multiplexer #(.select(1), .width(8)) multiplexer_1 (.in0(E), .in1(A), .out(multiplexer_1_out));  // open: sel
  Multiplexer #(.select(1), .width(8)) multiplexer_2 (.in0(B), .in1(F), .out(multiplexer_2_out));  // open: sel
  Adder #(.width(8)) adder_1 (.a(multiplexer_1_out), .b(multiplexer_2_out), .out(E));  // open: cin, cout
  Adder #(.width(8)) adder_2 (.a(C), .b(D), .out(F));  // open: cin, cout
endmodule
